// Logisim project 00710740_a2b.circ as structural Verilog: 6 circuits, main circuit main
module main (
  input  ready,
  input  areset,
  output start,
  output [15:0] X
);

  wire clk_out, keyboard_1_avail, rpn_ascii2binary_1_read_enable;
  wire [6:0] keyboard_1_data;

  Keyboard keyboard_1 (
    .clk(clk_out), .re(rpn_ascii2binary_1_read_enable), .clr(areset), .avail(keyboard_1_avail),
    .data(keyboard_1_data));
  Clock clk (.out(clk_out));
  rpn_ascii2binary rpn_ascii2binary_1 (
    .\input (keyboard_1_data), .available(keyboard_1_avail), .\output (X),
    .read_enable(rpn_ascii2binary_1_read_enable), .clk(clk_out), .areset(areset), .start(start), .ready(ready));
  // Probe on X
endmodule

// a2b
module rpn_ascii2binary (
  input  [6:0] \input ,
  input  available,
  input  ready,
  input  clk,
  input  areset,
  output start,
  output [15:0] \output ,
  output read_enable
);

  wire check_digit_cd0, check_digit_cd1, check_digit_cd2, logic_control_1_add, logic_control_1_m_en,
       logic_control_1_multi, logic_control_1_x_en, logic_control_1_zero;

  check_digit check_digit (.\input (\input ), .cd0(check_digit_cd0), .cd1(check_digit_cd1), .cd2(check_digit_cd2));
  logic_control logic_control_1 (
    .av(available), .read_enable(read_enable), .cd0(check_digit_cd0), .cd1(check_digit_cd1),
    .multi(logic_control_1_multi), .cd2(check_digit_cd2), .ready(ready), .zero(logic_control_1_zero),
    .add(logic_control_1_add), .X_en(logic_control_1_x_en), .M_en(logic_control_1_m_en), .start(start),
    .clk(clk), .areset(areset));
  datapath datapath_1 (
    .\input (\input ), .multi(logic_control_1_multi), .zero(logic_control_1_zero), .add(logic_control_1_add),
    .X_en(logic_control_1_x_en), .M_en(logic_control_1_m_en), .clk(clk), .areset(areset), .\output (\output ));
endmodule

module logic_control (
  input  av,
  input  cd0,
  input  cd1,
  input  cd2,
  input  ready,
  input  clk,
  input  areset,
  output read_enable,
  output multi,
  output zero,
  output add,
  output X_en,
  output M_en,
  output start
);

  wire and_1_out, and_5_out, and_6_out, and_7_out, and_8_out, and_9_out, and_10_out, and_12_out, and_13_out,
       and_14_out, and_15_out, and_16_out, and_17_out, and_18_out, and_19_out, and_20_out, and_21_out,
       and_22_out, and_23_out, and_24_out, and_25_out, and_26_out, and_27_out, and_28_out, and_29_out,
       and_30_out, and_31_out, and_33_out, and_34_out, and_35_out, and_36_out, and_37_out, and_38_out,
       and_39_out, and_40_out, and_41_out, and_42_out, and_43_out, and_44_out, fd_2_q, fd_q, not_1_out,
       not_2_out, not_3_out, not_4_out, not_5_out, not_6_out, not_7_out, not_8_out, not_9_out, not_10_out,
       not_11_out, not_12_out, not_13_out, not_14_out, not_15_out, not_16_out, not_17_out, not_18_out,
       not_19_out, not_20_out, not_21_out, not_22_out, not_23_out, not_24_out, not_25_out, not_26_out,
       not_27_out, not_28_out, not_29_out, not_30_out, not_31_out, not_32_out, not_33_out, not_34_out,
       not_35_out, not_36_out, not_37_out, not_38_out, not_39_out, not_40_out, not_41_out, not_42_out,
       not_43_out, not_44_out, not_45_out, not_46_out, not_47_out, not_48_out, not_49_out, not_50_out,
       not_51_out, not_52_out, not_53_out, not_54_out, not_55_out, not_56_out, not_57_out, not_58_out,
       not_59_out, not_60_out, not_61_out, not_62_out, not_63_out, not_64_out, not_65_out, not_66_out,
       not_67_out, or_1_out, or_4_out, or_5_out, or_6_out, or_7_out, or_8_out, or_9_out, or_10_out, s0_q,
       s1_q, s2_q;

  not not_1 (not_1_out, fd_2_q);
  and and_1 (and_1_out, fd_2_q, ready);
  and and_2 (multi, s0_q, s1_q, not_2_out);
  not not_2 (not_2_out, s2_q);
  not not_3 (not_3_out, s0_q);
  and and_3 (zero, not_3_out, s1_q, not_4_out);
  not not_4 (not_4_out, s2_q);
  not not_5 (not_5_out, s0_q);
  and and_4 (add, not_5_out, s1_q, s2_q);
  and and_5 (and_5_out, s0_q, s1_q, not_6_out);
  not not_6 (not_6_out, s2_q);
  not not_7 (not_7_out, s0_q);
  and and_6 (and_6_out, not_7_out, s1_q, not_8_out);
  not not_8 (not_8_out, s2_q);
  not not_9 (not_9_out, s0_q);
  not not_10 (not_10_out, s1_q);
  and and_7 (and_7_out, not_9_out, not_10_out, s2_q);
  not not_11 (not_11_out, s0_q);
  and and_8 (and_8_out, not_11_out, s1_q, s2_q);
  not not_12 (not_12_out, s1_q);
  and and_9 (and_9_out, s0_q, not_12_out, s2_q);
  not not_13 (not_13_out, s0_q);
  and and_10 (and_10_out, not_13_out, s1_q, s2_q);
  and and_11 (start, s0_q, s1_q, s2_q, fd_2_q);
  not not_14 (not_14_out, s0_q);
  not not_15 (not_15_out, s2_q);
  not not_16 (not_16_out, s0_q);
  not not_17 (not_17_out, s1_q);
  not not_18 (not_18_out, s0_q);
  not not_19 (not_19_out, s1_q);
  not not_20 (not_20_out, s2_q);
  not not_21 (not_21_out, s0_q);
  not not_22 (not_22_out, s1_q);
  not not_23 (not_23_out, s2_q);
  not not_24 (not_24_out, s2_q);
  not not_25 (not_25_out, s0_q);
  not not_26 (not_26_out, s1_q);
  not not_27 (not_27_out, s0_q);
  not not_28 (not_28_out, s1_q);
  not not_29 (not_29_out, s2_q);
  not not_30 (not_30_out, s1_q);
  not not_31 (not_31_out, s2_q);
  not not_32 (not_32_out, cd1);
  not not_33 (not_33_out, cd2);
  not not_34 (not_34_out, s1_q);
  not not_35 (not_35_out, s2_q);
  not not_36 (not_36_out, cd0);
  not not_37 (not_37_out, cd2);
  not not_38 (not_38_out, s0_q);
  not not_39 (not_39_out, s1_q);
  not not_40 (not_40_out, s1_q);
  not not_41 (not_41_out, s0_q);
  not not_42 (not_42_out, ready);
  not not_43 (not_43_out, cd1);
  and and_12 (and_12_out, cd0, not_43_out, not_44_out);
  not not_44 (not_44_out, cd2);
  not not_45 (not_45_out, cd0);
  not not_46 (not_46_out, cd1);
  and and_13 (and_13_out, not_45_out, not_46_out, cd2);
  not not_47 (not_47_out, cd0);
  and and_14 (and_14_out, not_47_out, cd1, not_48_out);
  not not_48 (not_48_out, cd2);
  not not_49 (not_49_out, cd0);
  not not_50 (not_50_out, cd1);
  and and_15 (and_15_out, not_49_out, not_50_out, cd2);
  or or_1 (or_1_out, not_1_out, and_1_out);
  or or_2 (X_en, and_5_out, and_6_out, and_7_out, and_8_out);
  or or_3 (M_en, and_9_out, and_10_out);
  and and_16 (and_16_out, not_14_out, s1_q, not_15_out);
  and and_17 (and_17_out, not_16_out, not_17_out, s2_q);
  and and_18 (and_18_out, s0_q, s1_q, s2_q, fd_q);
  and and_19 (and_19_out, not_18_out, not_19_out, not_20_out, fd_q);
  and and_20 (and_20_out, not_21_out, not_22_out, not_23_out, fd_q);
  and and_21 (and_21_out, s0_q, s1_q, not_24_out, fd_q);
  and and_22 (and_22_out, not_25_out, s1_q, s2_q);
  or or_4 (or_4_out, and_22_out, and_23_out, and_24_out);
  and and_23 (and_23_out, s0_q, not_26_out, s2_q, fd_2_q);
  and and_24 (and_24_out, s0_q, s1_q, s2_q, fd_2_q);
  and and_25 (and_25_out, not_27_out, not_28_out, not_29_out, av);
  and and_26 (and_26_out, s0_q, not_30_out, not_31_out, cd0, not_32_out, not_33_out, fd_q);
  and and_27 (and_27_out, s0_q, not_34_out, not_35_out, not_36_out, cd1, not_37_out);
  and and_28 (and_28_out, not_38_out, not_39_out, s2_q);
  and and_29 (and_29_out, s0_q, not_40_out, s2_q);
  and and_30 (and_30_out, not_41_out, s1_q, s2_q);
  and and_31 (and_31_out, s0_q, s1_q, s2_q, fd_2_q, not_42_out);
  not not_51 (not_51_out, s1_q);
  not not_52 (not_52_out, s2_q);
  or or_5 (or_5_out, and_12_out, and_13_out);
  not not_53 (not_53_out, s0_q);
  not not_54 (not_54_out, s1_q);
  not not_55 (not_55_out, s1_q);
  not not_56 (not_56_out, ready);
  not not_57 (not_57_out, s2_q);
  not not_58 (not_58_out, s0_q);
  not not_59 (not_59_out, s2_q);
  not not_60 (not_60_out, s1_q);
  not not_61 (not_61_out, s2_q);
  or or_6 (or_6_out, and_14_out, and_15_out);
  not not_62 (not_62_out, s0_q);
  not not_63 (not_63_out, s1_q);
  not not_64 (not_64_out, s1_q);
  not not_65 (not_65_out, s0_q);
  not not_66 (not_66_out, s0_q);
  not not_67 (not_67_out, ready);
  and and_32 (read_enable, s0_q, s1_q, s2_q, or_1_out);
  or or_7 (or_7_out, and_16_out, and_17_out, and_18_out, and_19_out, and_20_out, and_21_out);
  or or_8 (or_8_out, and_25_out, and_26_out, and_27_out, and_28_out, and_29_out, and_30_out, and_31_out);
  and and_33 (and_33_out, s0_q, not_51_out, not_52_out, or_5_out);
  and and_34 (and_34_out, not_53_out, not_54_out, s2_q);
  and and_35 (and_35_out, s0_q, not_55_out, s2_q);
  and and_36 (and_36_out, s0_q, s1_q, s2_q, fd_2_q, not_56_out);
  and and_37 (and_37_out, s0_q, s1_q, not_57_out);
  and and_38 (and_38_out, not_58_out, s1_q, not_59_out);
  and and_39 (and_39_out, s0_q, not_60_out, not_61_out, or_6_out);
  and and_40 (and_40_out, not_62_out, not_63_out, s2_q);
  and and_41 (and_41_out, s0_q, not_64_out, s2_q);
  and and_42 (and_42_out, not_65_out, s1_q, s2_q);
  and and_43 (and_43_out, not_66_out, s1_q, s2_q);
  and and_44 (and_44_out, s0_q, s1_q, s2_q, fd_2_q, not_67_out);
  or or_9 (or_9_out, and_33_out, and_34_out, and_35_out, and_36_out);
  D_Flip_Flop fd (.clk(clk), .D(or_7_out), .Q(fd_q), .reset(areset));  // open: Qn, preset, en
  D_Flip_Flop fd_2 (.clk(clk), .D(or_4_out), .Q(fd_2_q), .reset(areset));  // open: Qn, preset, en
  D_Flip_Flop s0 (.clk(clk), .D(or_8_out), .Q(s0_q), .reset(areset));  // open: Qn, preset, en
  D_Flip_Flop s1 (.clk(clk), .D(or_9_out), .Q(s1_q), .reset(areset));  // open: Qn, preset, en
  D_Flip_Flop s2 (.clk(clk), .D(or_10_out), .Q(s2_q), .reset(areset));  // open: Qn, preset, en
  or or_10 (or_10_out, and_37_out, and_38_out, and_39_out, and_40_out, and_41_out, and_42_out, and_43_out, and_44_out);
endmodule

module datapath (
  input  [6:0] \input ,
  input  multi,
  input  zero,
  input  add,
  input  X_en,
  input  M_en,
  input  clk,
  input  areset,
  output [15:0] \output 
);

  wire [15:0] adder_1_out, adder_2_out, bit_extender_1_out, M_q, multiplexer_1_out, multiplexer_2_out,
       multiplexer_3_out, multiplier_1_out_2;

  assign bit_extender_1_out = {{12{1'b0}}, \input [3:0]};  // Bit_Extender bit_extender_1
  Adder #(.width(16)) adder_1 (.a(\output ), .b(bit_extender_1_out), .out(adder_1_out));  // open: cin, cout
  Adder #(.width(16)) adder_2 (.a(\output ), .b(M_q), .out(adder_2_out));  // open: cin, cout
  Multiplexer #(.width(16), .enable("false")) multiplexer_1 (
    .in0(adder_1_out), .in1(adder_2_out), .out(multiplexer_1_out), .sel(add));
  Multiplexer #(.width(16), .enable("false")) multiplexer_2 (
    .in0(multiplexer_1_out), .in1({16{1'b0}}), .out(multiplexer_2_out), .sel(zero));
  Multiplexer #(.width(16), .enable("false")) multiplexer_3 (
    .in0(multiplexer_2_out), .in1(multiplier_1_out_2), .out(multiplexer_3_out), .sel(multi));
  multiplier multiplier_1 (.in_1(\output ), .out_2(multiplier_1_out_2));
  Register #(.width(16)) X (.D(multiplexer_3_out), .en(X_en), .Q(\output ), .clk(clk), .clr(areset));
  Register #(.width(16)) M (.D(\output ), .en(M_en), .Q(M_q), .clk(clk), .clr(areset));
endmodule

module check_digit (
  input  [6:0] \input ,
  output cd0,
  output cd1,
  output cd2
);

  wire comparator_1_lt, comparator_2_gt;

  Comparator #(.width(7)) comparator_1 (.a(\input ), .b(7'b0111010), .lt(comparator_1_lt));  // open: gt, eq
  Comparator #(.width(7)) comparator_2 (.a(\input ), .b(7'b0101111), .gt(comparator_2_gt));  // open: eq, lt
  Comparator #(.width(7)) comparator_3 (.a(\input ), .b(7'b0001010), .eq(cd1));  // open: gt, lt
  Comparator #(.width(7)) comparator_4 (.a(\input ), .b(7'b0101011), .eq(cd2));  // open: gt, lt
  and and_1 (cd0, comparator_1_lt, comparator_2_gt);
endmodule

// multi
module multiplier (
  input  [15:0] in_1,
  output [15:0] out_2
);

  wire [15:0] adder_1_out, adder_2_out, adder_3_out, adder_4_out, adder_5_out, adder_6_out, adder_7_out,
       adder_8_out;

  Adder #(.width(16)) adder_1 (.a(in_1), .b(in_1), .out(adder_1_out));  // open: cin, cout
  Adder #(.width(16)) adder_2 (.a(in_1), .b(adder_1_out), .out(adder_2_out));  // open: cin, cout
  Adder #(.width(16)) adder_3 (.a(in_1), .b(adder_2_out), .out(adder_3_out));  // open: cin, cout
  Adder #(.width(16)) adder_4 (.a(in_1), .b(adder_3_out), .out(adder_4_out));  // open: cin, cout
  Adder #(.width(16)) adder_5 (.a(in_1), .b(adder_4_out), .out(adder_5_out));  // open: cin, cout
  Adder #(.width(16)) adder_6 (.a(in_1), .b(adder_5_out), .out(adder_6_out));  // open: cin, cout
  Adder #(.width(16)) adder_7 (.a(in_1), .b(adder_6_out), .out(adder_7_out));  // open: cin, cout
  Adder #(.width(16)) adder_8 (.a(in_1), .b(adder_7_out), .out(adder_8_out));  // open: cin, cout
  Adder #(.width(16)) adder_9 (.a(in_1), .b(adder_8_out), .out(out_2));  // open: cin, cout
endmodule
