// Logisim project binary2ascii.circ as structural Verilog: 8 circuits, main circuit main
module main (
  input  [15:0] Zahl,
  input  read_enable,
  input  start,
  input  areset,
  output ready
);

  wire binary2ascii_1_write_enable, clk_out;
  wire [6:0] binary2ascii_1_output, keyboard_1_data;

  Keyboard keyboard_1 (.clk(clk_out), .re(read_enable), .clr(areset), .data(keyboard_1_data));  // open: avail
  // Probe on Zahl
  Clock clk (.out(clk_out));
  binary2ascii binary2ascii_1 (
    .Zahl(Zahl), .keyboard(keyboard_1_data), .read_enable(read_enable), .start(start),
    .\output (binary2ascii_1_output), .write_enable(binary2ascii_1_write_enable), .ready(ready),
    .clk(clk_out), .areset(areset));
  TTY #(.cols(8)) tty_1 (.data(binary2ascii_1_output), .clk(clk_out), .we(binary2ascii_1_write_enable), .clr(areset));
endmodule

module binary2ascii (
  input  [15:0] Zahl,
  input  [6:0] keyboard,
  input  read_enable,
  input  start,
  input  clk,
  input  areset,
  output [6:0] \output ,
  output write_enable,
  output ready
);

  wire control_logic_1_nc, control_logic_1_nl, control_logic_1_ns, control_logic_1_pz_2, datapath_1_p_scnd_z,
       datapath_1_p_thrd_z, datapath_1_put_num, datapath_1_put_zero;

  control_logic control_logic_1 (
    .re(read_enable), .nc(control_logic_1_nc), .st(start), .pn(datapath_1_put_num), .ns(control_logic_1_ns),
    .pz(datapath_1_put_zero), .psz(datapath_1_p_scnd_z), .nl(control_logic_1_nl), .ptz(datapath_1_p_thrd_z),
    .pz_2(control_logic_1_pz_2), .pc(write_enable), .rd(ready), .clk(clk), .areset(areset));
  datapath datapath_1 (
    .keyboard(keyboard), .Zahl(Zahl), .read_enable(read_enable), .num_select(control_logic_1_ns),
    .put_newline(control_logic_1_nl), .digit(\output ), .put_num(datapath_1_put_num), .clk(clk),
    .areset(areset), .num_ctrl(control_logic_1_nc), .put_zero(datapath_1_put_zero),
    .zero(control_logic_1_pz_2), .p_scnd_z(datapath_1_p_scnd_z), .p_thrd_z(datapath_1_p_thrd_z));
endmodule

module datapath (
  input  [15:0] Zahl,
  input  [6:0] keyboard,
  input  read_enable,
  input  num_ctrl,
  input  num_select,
  input  put_newline,
  input  zero,
  input  clk,
  input  areset,
  output [6:0] digit,
  output put_zero,
  output p_scnd_z,
  output p_thrd_z,
  output put_num
);

  wire read_check_1_rc0, read_check_1_rc1, read_check_1_rc2, read_check_1_rc3;
  wire [6:0] check_digit_1_output, multiplexer_2_out, multiplexer_3_out, multiplexer_4_out, read_set_1_digit;
  wire [15:0] check_digit_1_num_2, multiplexer_1_out, num_q, read_set_1_check, read_set_1_decrementor;

  Multiplexer #(.width(16), .enable("false")) multiplexer_1 (
    .in0(check_digit_1_num_2), .in1(Zahl), .out(multiplexer_1_out), .sel(num_select));
  Register #(.width(16)) num (.D(multiplexer_1_out), .en(num_ctrl), .Q(num_q), .clk(clk), .clr(areset));
  read_check read_check_1 (
    .\input (num_q), .rc0(read_check_1_rc0), .rc1(read_check_1_rc1), .rc3(read_check_1_rc3),
    .rc2(read_check_1_rc2), .put_num(put_num));
  read_set read_set_1 (
    .rc0(read_check_1_rc0), .rc1(read_check_1_rc1), .rc2(read_check_1_rc2), .rc3(read_check_1_rc3),
    .\input (num_q), .check(read_set_1_check), .decrementor(read_set_1_decrementor),
    .digit(read_set_1_digit), .put_num(put_num));
  check_digit check_digit_1 (
    .num(num_q), .check(read_set_1_check), .decrementor(read_set_1_decrementor), .digit(read_set_1_digit),
    .\output (check_digit_1_output), .num_2(check_digit_1_num_2), .putzero(put_zero), .p_scnd_z(p_scnd_z),
    .p_thrd_z(p_thrd_z));
  Multiplexer #(.width(7), .enable("false")) multiplexer_2 (
    .in0(check_digit_1_output), .in1(read_set_1_digit), .out(multiplexer_2_out), .sel(put_num));
  Multiplexer #(.width(7), .enable("false")) multiplexer_3 (
    .in0(multiplexer_2_out), .in1(7'b0110000), .out(multiplexer_3_out), .sel(zero));
  Multiplexer #(.width(7), .enable("false")) multiplexer_4 (
    .in0(multiplexer_3_out), .in1(7'b0001010), .out(multiplexer_4_out), .sel(put_newline));
  Multiplexer #(.width(7), .enable("false")) multiplexer_5 (
    .in0(multiplexer_4_out), .in1(keyboard), .out(digit), .sel(read_enable));
endmodule

module control_logic (
  input  re,
  input  st,
  input  pn,
  input  pz,
  input  psz,
  input  ptz,
  input  clk,
  input  areset,
  output nc,
  output ns,
  output nl,
  output pz_2,
  output pc,
  output rd
);

  wire and_1_out, and_2_out, and_4_out, and_5_out, and_6_out, and_7_out, and_8_out, and_9_out, and_10_out,
       and_11_out, and_12_out, and_13_out, and_14_out, and_15_out, and_16_out, and_17_out, and_19_out,
       and_20_out, and_21_out, and_22_out, and_23_out, and_24_out, and_25_out, and_26_out, and_27_out,
       and_28_out, and_29_out, and_30_out, and_31_out, and_32_out, and_33_out, not_1_out, not_2_out,
       not_3_out, not_4_out, not_5_out, not_6_out, not_7_out, not_8_out, not_9_out, not_10_out, not_11_out,
       not_12_out, not_13_out, not_14_out, not_15_out, not_16_out, not_17_out, not_18_out, not_19_out,
       not_20_out, not_21_out, not_22_out, not_23_out, not_24_out, not_25_out, not_26_out, not_27_out,
       not_28_out, not_29_out, not_30_out, not_31_out, not_32_out, not_33_out, not_34_out, not_35_out,
       not_36_out, not_37_out, not_38_out, not_39_out, not_40_out, not_41_out, not_42_out, not_43_out,
       not_44_out, not_45_out, not_46_out, not_47_out, not_48_out, not_49_out, or_1_out, or_5_out, or_6_out,
       or_8_out, or_9_out, or_10_out, s0_q, s1_q, s2_q;

  not not_1 (not_1_out, s1_q);
  not not_2 (not_2_out, s2_q);
  not not_3 (not_3_out, s0_q);
  not not_4 (not_4_out, s2_q);
  not not_5 (not_5_out, s1_q);
  not not_6 (not_6_out, s2_q);
  not not_7 (not_7_out, s2_q);
  not not_8 (not_8_out, s1_q);
  not not_9 (not_9_out, s2_q);
  not not_10 (not_10_out, s1_q);
  not not_11 (not_11_out, s1_q);
  not not_12 (not_12_out, s0_q);
  not not_13 (not_13_out, s0_q);
  not not_14 (not_14_out, s1_q);
  not not_15 (not_15_out, s2_q);
  not not_16 (not_16_out, s0_q);
  not not_17 (not_17_out, s1_q);
  not not_18 (not_18_out, psz);
  not not_19 (not_19_out, psz);
  not not_20 (not_20_out, pz);
  and and_1 (and_1_out, s0_q, not_1_out, not_2_out);
  and and_2 (and_2_out, not_3_out, s1_q, not_4_out);
  and and_3 (ns, s0_q, not_5_out, not_6_out);
  and and_4 (and_4_out, s0_q, s1_q, not_7_out);
  and and_5 (and_5_out, s0_q, not_8_out, not_9_out);
  and and_6 (and_6_out, s0_q, not_10_out, s2_q);
  and and_7 (and_7_out, s0_q, not_11_out, s2_q);
  and and_8 (and_8_out, not_12_out, s1_q, s2_q);
  and and_9 (and_9_out, s0_q, s1_q, s2_q);
  and and_10 (and_10_out, s0_q, s1_q, not_21_out);
  not not_21 (not_21_out, s2_q);
  and and_11 (and_11_out, s0_q, not_22_out, not_23_out);
  not not_22 (not_22_out, s1_q);
  not not_23 (not_23_out, s2_q);
  and and_12 (and_12_out, s0_q, s1_q, not_24_out);
  not not_24 (not_24_out, s2_q);
  and and_13 (and_13_out, not_13_out, not_14_out, not_15_out, re);
  not not_25 (not_25_out, s1_q);
  and and_14 (and_14_out, s0_q, not_25_out, s2_q);
  not not_26 (not_26_out, s0_q);
  and and_15 (and_15_out, not_26_out, s1_q, s2_q);
  and and_16 (and_16_out, s0_q, s1_q, s2_q);
  not not_27 (not_27_out, s0_q);
  and and_17 (and_17_out, not_27_out, s1_q, not_28_out);
  not not_28 (not_28_out, s2_q);
  and and_18 (rd, not_16_out, not_17_out, s2_q);
  and and_19 (and_19_out, not_18_out, pz);
  and and_20 (and_20_out, pn, not_19_out);
  and and_21 (and_21_out, pn, not_20_out);
  not not_29 (not_29_out, s0_q);
  not not_30 (not_30_out, s2_q);
  or or_1 (or_1_out, ptz, psz, pz);
  not not_31 (not_31_out, s0_q);
  not not_32 (not_32_out, s2_q);
  or or_2 (nc, and_1_out, and_2_out);
  or or_3 (nl, and_4_out, and_5_out);
  or or_4 (pz_2, and_6_out, and_7_out, and_8_out, and_9_out);
  not not_33 (not_33_out, s0_q);
  not not_34 (not_34_out, s1_q);
  not not_35 (not_35_out, s2_q);
  not not_36 (not_36_out, s0_q);
  not not_37 (not_37_out, s2_q);
  or or_5 (or_5_out, ptz, and_19_out, and_20_out);
  not not_38 (not_38_out, s0_q);
  not not_39 (not_39_out, s1_q);
  not not_40 (not_40_out, s2_q);
  not not_41 (not_41_out, s0_q);
  not not_42 (not_42_out, s2_q);
  or or_6 (or_6_out, ptz, psz, and_21_out);
  not not_43 (not_43_out, s1_q);
  not not_44 (not_44_out, s0_q);
  not not_45 (not_45_out, s2_q);
  not not_46 (not_46_out, ptz);
  not not_47 (not_47_out, psz);
  not not_48 (not_48_out, pz);
  not not_49 (not_49_out, pn);
  and and_22 (and_22_out, not_29_out, s1_q, not_30_out, or_1_out);
  and and_23 (and_23_out, s0_q, s1_q, s2_q);
  and and_24 (and_24_out, not_31_out, s1_q, s2_q);
  and and_25 (and_25_out, s0_q, s1_q, not_32_out);
  or or_7 (pc, and_10_out, and_11_out, and_12_out, and_13_out, and_14_out, and_15_out, and_16_out, and_17_out);
  and and_26 (and_26_out, not_33_out, not_34_out, not_35_out, st);
  and and_27 (and_27_out, not_36_out, s1_q, not_37_out, or_5_out);
  and and_28 (and_28_out, not_38_out, s1_q, s2_q);
  and and_29 (and_29_out, s0_q, not_39_out, not_40_out);
  and and_30 (and_30_out, not_41_out, s1_q, not_42_out, or_6_out);
  and and_31 (and_31_out, s0_q, s1_q, s2_q);
  and and_32 (and_32_out, s0_q, not_43_out, s2_q);
  and and_33 (and_33_out, not_44_out, s1_q, not_45_out, not_46_out, not_47_out, not_48_out, not_49_out);
  or or_8 (or_8_out, and_22_out, and_23_out, and_24_out, and_25_out);
  or or_9 (or_9_out, and_26_out, and_27_out, and_28_out);
  or or_10 (or_10_out, and_29_out, and_30_out, and_31_out, and_32_out, and_33_out);
  D_Flip_Flop s0 (.clk(clk), .D(or_9_out), .Q(s0_q), .reset(areset));  // open: Qn, preset, en
  D_Flip_Flop s1 (.clk(clk), .D(or_10_out), .Q(s1_q), .reset(areset));  // open: Qn, preset, en
  D_Flip_Flop s2 (.clk(clk), .D(or_8_out), .Q(s2_q), .reset(areset));  // open: Qn, preset, en
endmodule

module read_check (
  input  [15:0] \input ,
  output rc0,
  output rc1,
  output rc2,
  output rc3,
  output put_num
);

  wire comparator_4_eq, comparator_4_lt;

  Comparator #(.width(16), .mode("unsigned")) comparator_1 (.a(\input ), .b(16'h270f), .gt(rc0));  // open: eq, lt
  Comparator #(.width(16), .mode("unsigned")) comparator_2 (.a(\input ), .b(16'h3e7), .gt(rc1));  // open: eq, lt
  Comparator #(.width(16), .mode("unsigned")) comparator_3 (.a(\input ), .b(16'h63), .gt(rc2));  // open: eq, lt
  Comparator #(.width(16), .mode("unsigned")) comparator_4 (
    .a(\input ), .b(16'h9), .gt(rc3), .eq(comparator_4_eq), .lt(comparator_4_lt));
  or or_1 (put_num, comparator_4_eq, comparator_4_lt);
endmodule

module read_set (
  input  [15:0] \input ,
  input  rc0,
  input  rc1,
  input  rc2,
  input  rc3,
  input  put_num,
  output [15:0] check,
  output [15:0] decrementor,
  output [6:0] digit
);

  wire [1:0] rs_logic_1_out_5;
  wire [6:0] adder_1_out, bit_extender_1_out, multiplexer_2_out;

  rs_logic rs_logic_1 (.rc3(rc0), .rc2(rc1), .rc1(rc2), .rc0(rc3), .out_5(rs_logic_1_out_5));
  Bit_Extender #(.in_width(16), .out_width(7)) bit_extender_1 (.in(\input ), .out(bit_extender_1_out));
  Multiplexer #(.select(2), .width(16), .enable("false")) multiplexer_1 (
    .in0(16'hea5f), .in1(16'h2327), .in2(16'h383), .in3(16'h59), .out(check), .sel(rs_logic_1_out_5));
  Adder #(.width(7)) adder_1 (.a(bit_extender_1_out), .b(7'b0110000), .out(adder_1_out));  // open: cin, cout
  Multiplexer #(.width(7), .enable("false")) multiplexer_2 (
    .in0(7'b0111001), .in1(adder_1_out), .out(multiplexer_2_out), .sel(put_num));
  Multiplexer #(.width(7), .enable("false")) multiplexer_3 (
    .in0(multiplexer_2_out), .in1(7'b0110110), .out(digit), .sel(rc0));
  Multiplexer #(.select(2), .width(16), .enable("false")) multiplexer_4 (
    .in0(16'h2710), .in1(16'h3e8), .in2(16'h64), .in3(16'ha), .out(decrementor), .sel(rs_logic_1_out_5));
endmodule

module rs_logic (
  input  rc3,
  input  rc2,
  input  rc1,
  input  rc0,
  output [1:0] out_5
);

  wire and_1_out, and_2_out, and_3_out, and_4_out, not_1_out, not_2_out, not_3_out, not_4_out, not_5_out,
       not_6_out, not_7_out, not_8_out, not_9_out, or_1_out, or_2_out;
  wire [1:0] bit_extender_1_out, bit_extender_2_out, shifter_1_out;

  not not_1 (not_1_out, rc2);
  not not_2 (not_2_out, rc3);
  not not_3 (not_3_out, rc1);
  not not_4 (not_4_out, rc2);
  not not_5 (not_5_out, rc3);
  not not_6 (not_6_out, rc3);
  not not_7 (not_7_out, rc1);
  not not_8 (not_8_out, rc2);
  not not_9 (not_9_out, rc3);
  and and_1 (and_1_out, rc0, rc1, not_1_out, not_2_out);
  or or_1 (or_1_out, and_1_out, and_2_out);
  and and_2 (and_2_out, rc0, not_3_out, not_4_out, not_5_out);
  and and_3 (and_3_out, rc0, rc1, rc2, not_6_out);
  or or_2 (or_2_out, and_3_out, and_4_out);
  and and_4 (and_4_out, rc0, not_7_out, not_8_out, not_9_out);
  assign bit_extender_1_out = {{1{1'b0}}, or_1_out};  // Bit_Extender bit_extender_1
  assign bit_extender_2_out = {{1{1'b0}}, or_2_out};  // Bit_Extender bit_extender_2
  Shifter #(.width(2)) shifter_1 (.in(bit_extender_1_out), .\dist (1'b1), .out(shifter_1_out));
  Adder #(.width(2)) adder_1 (.a(shifter_1_out), .b(bit_extender_2_out), .out(out_5));  // open: cin, cout
endmodule

module check_digit (
  input  [15:0] num,
  input  [15:0] check,
  input  [15:0] decrementor,
  input  [6:0] digit,
  output [15:0] num_2,
  output putzero,
  output p_scnd_z,
  output p_thrd_z,
  output [6:0] \output 
);

  wire comparator_1_gt, comparator_2_gt, comparator_3_gt, comparator_4_gt, comparator_5_gt, comparator_6_gt,
       comparator_7_gt, comparator_8_gt, comparator_9_gt, comparator_10_gt, comparator_11_gt;
  wire [6:0] multiplexer_7_out, multiplexer_10_out, multiplexer_14_out, multiplexer_15_out,
       multiplexer_19_out, multiplexer_20_out, multiplexer_21_out, subtractor_3_out, subtractor_5_out,
       subtractor_7_out, subtractor_10_out, subtractor_11_out, subtractor_13_out, subtractor_15_out,
       subtractor_16_out;
  wire [15:0] multiplexer_1_out, multiplexer_2_out, multiplexer_3_out, multiplexer_4_out, multiplexer_5_out,
       multiplexer_6_out, multiplexer_8_out, multiplexer_9_out, multiplexer_11_out, multiplexer_12_out,
       multiplexer_13_out, multiplexer_16_out, multiplexer_17_out, multiplexer_18_out, subtractor_1_out,
       subtractor_2_out, subtractor_4_out, subtractor_6_out, subtractor_8_out, subtractor_9_out,
       subtractor_12_out, subtractor_14_out, subtractor_17_out;

  Comparator #(.width(16), .mode("unsigned")) comparator_1 (.a(num), .b(check), .gt(comparator_1_gt));  // open: eq, lt
  Subtractor #(.width(16)) subtractor_1 (.a(decrementor), .b(16'h1), .out(subtractor_1_out));  // open: bin, bout
  Comparator #(.width(16), .mode("unsigned")) comparator_2 (
    .a(num), .b(subtractor_2_out), .gt(comparator_2_gt));  // open: eq, lt
  Subtractor #(.width(16)) subtractor_2 (.a(check), .b(decrementor), .out(subtractor_2_out));  // open: bin, bout
  Subtractor #(.width(7)) subtractor_3 (.a(digit), .b(7'b0000001), .out(subtractor_3_out));  // open: bin, bout
  Comparator #(.width(16), .mode("unsigned")) comparator_3 (
    .a(num), .b(subtractor_4_out), .gt(comparator_3_gt));  // open: eq, lt
  Subtractor #(.width(16)) subtractor_4 (
    .a(subtractor_2_out), .b(decrementor), .out(subtractor_4_out));  // open: bin, bout
  Subtractor #(.width(7)) subtractor_5 (
    .a(subtractor_3_out), .b(7'b0000001), .out(subtractor_5_out));  // open: bin, bout
  Comparator #(.width(16), .mode("unsigned")) comparator_4 (
    .a(num), .b(subtractor_6_out), .gt(comparator_4_gt));  // open: eq, lt
  Subtractor #(.width(16)) subtractor_6 (
    .a(subtractor_4_out), .b(decrementor), .out(subtractor_6_out));  // open: bin, bout
  Subtractor #(.width(7)) subtractor_7 (
    .a(subtractor_5_out), .b(7'b0000001), .out(subtractor_7_out));  // open: bin, bout
  Comparator #(.width(16), .mode("unsigned")) comparator_5 (
    .a(num), .b(subtractor_8_out), .gt(comparator_5_gt));  // open: eq, lt
  Subtractor #(.width(16)) subtractor_8 (
    .a(subtractor_6_out), .b(decrementor), .out(subtractor_8_out));  // open: bin, bout
  Subtractor #(.width(16)) subtractor_9 (
    .a(subtractor_8_out), .b(decrementor), .out(subtractor_9_out));  // open: bin, bout
  Subtractor #(.width(7)) subtractor_10 (
    .a(subtractor_7_out), .b(7'b0000001), .out(subtractor_10_out));  // open: bin, bout
  Comparator #(.width(16), .mode("unsigned")) comparator_6 (
    .a(num), .b(subtractor_9_out), .gt(comparator_6_gt));  // open: eq, lt
  Subtractor #(.width(7)) subtractor_11 (
    .a(subtractor_10_out), .b(7'b0000001), .out(subtractor_11_out));  // open: bin, bout
  Comparator #(.width(16), .mode("unsigned")) comparator_7 (
    .a(num), .b(subtractor_12_out), .gt(comparator_7_gt));  // open: eq, lt
  Subtractor #(.width(16)) subtractor_12 (
    .a(subtractor_9_out), .b(decrementor), .out(subtractor_12_out));  // open: bin, bout
  Subtractor #(.width(7)) subtractor_13 (
    .a(subtractor_11_out), .b(7'b0000001), .out(subtractor_13_out));  // open: bin, bout
  Comparator #(.width(16), .mode("unsigned")) comparator_8 (
    .a(num), .b(subtractor_14_out), .gt(comparator_8_gt));  // open: eq, lt
  Subtractor #(.width(16)) subtractor_14 (
    .a(subtractor_12_out), .b(decrementor), .out(subtractor_14_out));  // open: bin, bout
  Subtractor #(.width(7)) subtractor_15 (
    .a(subtractor_13_out), .b(7'b0000001), .out(subtractor_15_out));  // open: bin, bout
  Multiplexer #(.width(16), .enable("false")) multiplexer_1 (
    .in0(subtractor_1_out), .in1(subtractor_14_out), .out(multiplexer_1_out), .sel(comparator_8_gt));
  Multiplexer #(.width(16), .enable("false")) multiplexer_2 (
    .in0(multiplexer_1_out), .in1(subtractor_12_out), .out(multiplexer_2_out), .sel(comparator_7_gt));
  Comparator #(.width(16), .mode("unsigned")) comparator_9 (
    .a(decrementor), .b(16'h270f), .gt(comparator_9_gt));  // open: eq, lt
  Subtractor #(.width(7)) subtractor_16 (
    .a(subtractor_15_out), .b(7'b0000001), .out(subtractor_16_out));  // open: bin, bout
  Multiplexer #(.width(16), .enable("false")) multiplexer_3 (
    .in0(multiplexer_2_out), .in1(subtractor_9_out), .out(multiplexer_3_out), .sel(comparator_6_gt));
  Comparator #(.width(16), .mode("unsigned")) comparator_10 (
    .a(decrementor), .b(16'h3e7), .gt(comparator_10_gt));  // open: eq, lt
  Multiplexer #(.width(16), .enable("false")) multiplexer_4 (
    .in0(multiplexer_3_out), .in1(subtractor_8_out), .out(multiplexer_4_out), .sel(comparator_5_gt));
  Multiplexer #(.width(16), .enable("false")) multiplexer_5 (
    .in0(multiplexer_4_out), .in1(subtractor_6_out), .out(multiplexer_5_out), .sel(comparator_4_gt));
  Multiplexer #(.width(16), .enable("false")) multiplexer_6 (
    .in0(multiplexer_5_out), .in1(subtractor_4_out), .out(multiplexer_6_out), .sel(comparator_3_gt));
  Comparator #(.width(16), .mode("unsigned")) comparator_11 (
    .a(decrementor), .b(16'h63), .gt(comparator_11_gt));  // open: eq, lt
  Multiplexer #(.width(7), .enable("false")) multiplexer_7 (
    .in0(subtractor_16_out), .in1(subtractor_15_out), .out(multiplexer_7_out), .sel(comparator_8_gt));
  Multiplexer #(.width(16), .enable("false")) multiplexer_8 (
    .in0(multiplexer_6_out), .in1(subtractor_2_out), .out(multiplexer_8_out), .sel(comparator_2_gt));
  Multiplexer #(.width(16), .enable("false")) multiplexer_9 (
    .in0({16{1'b0}}), .in1(16'ha), .out(multiplexer_9_out), .sel(comparator_11_gt));
  Multiplexer #(.width(7), .enable("false")) multiplexer_10 (
    .in0(multiplexer_7_out), .in1(subtractor_13_out), .out(multiplexer_10_out), .sel(comparator_7_gt));
  Multiplexer #(.width(16), .enable("false")) multiplexer_11 (
    .in0(multiplexer_8_out), .in1(check), .out(multiplexer_11_out), .sel(comparator_1_gt));
  Multiplexer #(.width(16), .enable("false")) multiplexer_12 (
    .in0(multiplexer_9_out), .in1(16'h64), .out(multiplexer_12_out), .sel(comparator_10_gt));
  Multiplexer #(.width(16), .enable("false")) multiplexer_13 (
    .in0({16{1'b0}}), .in1(16'ha), .out(multiplexer_13_out), .sel(comparator_10_gt));
  Multiplexer #(.width(7), .enable("false")) multiplexer_14 (
    .in0(multiplexer_10_out), .in1(subtractor_11_out), .out(multiplexer_14_out), .sel(comparator_6_gt));
  Multiplexer #(.width(7), .enable("false")) multiplexer_15 (
    .in0(multiplexer_14_out), .in1(subtractor_10_out), .out(multiplexer_15_out), .sel(comparator_5_gt));
  Subtractor #(.width(16)) subtractor_17 (.a(num), .b(multiplexer_11_out), .out(subtractor_17_out));  // open: bin, bout
  Multiplexer #(.width(16), .enable("false")) multiplexer_16 (
    .in0(multiplexer_12_out), .in1(16'h3e8), .out(multiplexer_16_out), .sel(comparator_9_gt));
  Multiplexer #(.width(16), .enable("false")) multiplexer_17 (
    .in0(multiplexer_13_out), .in1(16'h64), .out(multiplexer_17_out), .sel(comparator_9_gt));
  Multiplexer #(.width(16), .enable("false")) multiplexer_18 (
    .in0({16{1'b0}}), .in1(16'ha), .out(multiplexer_18_out), .sel(comparator_9_gt));
  Multiplexer #(.width(7), .enable("false")) multiplexer_19 (
    .in0(multiplexer_15_out), .in1(subtractor_7_out), .out(multiplexer_19_out), .sel(comparator_4_gt));
  Multiplexer #(.width(7), .enable("false")) multiplexer_20 (
    .in0(multiplexer_19_out), .in1(subtractor_5_out), .out(multiplexer_20_out), .sel(comparator_3_gt));
  Subtractor #(.width(16)) subtractor_18 (.a(subtractor_17_out), .b(16'h1), .out(num_2));  // open: bin, bout
  Comparator #(.width(16), .mode("unsigned")) comparator_12 (
    .a(num_2), .b(multiplexer_16_out), .lt(putzero));  // open: gt, eq
  Comparator #(.width(16), .mode("unsigned")) comparator_13 (
    .a(num_2), .b(multiplexer_17_out), .lt(p_scnd_z));  // open: gt, eq
  Comparator #(.width(16), .mode("unsigned")) comparator_14 (
    .a(num_2), .b(multiplexer_18_out), .lt(p_thrd_z));  // open: gt, eq
  Multiplexer #(.width(7), .enable("false")) multiplexer_21 (
    .in0(multiplexer_20_out), .in1(subtractor_3_out), .out(multiplexer_21_out), .sel(comparator_2_gt));
  Multiplexer #(.width(7), .enable("false")) multiplexer_22 (
    .in0(multiplexer_21_out), .in1(digit), .out(\output ), .sel(comparator_1_gt));
endmodule
